// Logisim project CPU.circ as structural Verilog: 6 circuits, main circuit main
module main (
);

  wire ALUSrc, clk, Ifbeq, MemtoReg, MemWrite, RegDst, RegWrite, reset1, reset2, reset3, zero;
  wire [1:0] ALUOp, Extop;
  wire [4:0] multiplexer_1_out;
  wire [5:0] func;
  wire [15:6] imm16;
  wire [31:0] imm32, multiplexer_3_out, ram_1_data, RD1, RD2, result, WD;
  wire [31:16] Instr;

  Clock u_clk (.out(clk));
  Button reset (.out(reset1));
  Button reset_2 (.out(reset2));
  Button reset_3 (.out(reset3));
  IFU ifu_1 (.Instr({Instr, imm16, func}), .reset(reset1), .Ifbeq(Ifbeq), .zero(zero), .clk(clk));
  Controller controller_1 (
    .func(func), .op(Instr[31:26]), .RegDst(RegDst), .ALUSrc(ALUSrc), .MemtoReg(MemtoReg),
    .RegWrite(RegWrite), .Extop(Extop), .MemWrite(MemWrite), .Branch(Ifbeq), .ALUop(ALUOp));
  Multiplexer #(.width(5), .enable("false")) multiplexer_1 (
    .in0(Instr[20:16]), .in1(imm16[15:11]), .out(multiplexer_1_out), .sel(RegDst));
  GPR gpr_1 (
    .WD(WD), .A1(Instr[25:21]), .A2(Instr[20:16]), .A3(multiplexer_1_out), .RD1(RD1), .RD2(RD2),
    .WE(RegWrite), .reset(reset3));
  Extender extender_1 (.input16({imm16, func}), .output32(imm32), .Extop(Extop));
  RAM #(.addrWidth(5), .dataWidth(32), .bus("separate")) ram_1 (
    .addr(result[6:2]), .din(RD2), .data(ram_1_data), .str(MemWrite), .clk(clk), .clr(reset2));  // open: sel, ld
  Multiplexer #(.width(32), .enable("false")) multiplexer_2 (.in0(result), .in1(ram_1_data), .out(WD), .sel(MemtoReg));
  Multiplexer #(.width(32), .enable("false")) multiplexer_3 (
    .in0(RD2), .in1(imm32), .out(multiplexer_3_out), .sel(ALUSrc));
  ALU alu_1 (.inputA(RD1), .inputB(multiplexer_3_out), .ALUOp(ALUOp), .result(result), .zero(zero));

  // Other names for the same wires on the sheet: imm16[5:0] = func; Instr[15:0] = {imm16, func};
  //   Rd[4:0] = imm16[15:11]; Rt[4:0] = Instr[20:16]; Rs[4:0] = Instr[25:21]; op[5:0] = Instr[31:26]
endmodule

module IFU (
  input  Ifbeq,
  input  zero,
  input  clk,
  input  reset,
  output [31:0] Instr
);

  wire or_1_out;
  wire [4:0] register_1_q;
  wire [10:0] register_1_q_2;
  wire [13:0] register_1_q_3;
  wire [29:0] adder_1_out, adder_2_out, bit_extender_1_out, multiplexer_1_out;

  Register #(.width(30)) register_1 (
    .D(multiplexer_1_out), .Q({register_1_q_3, register_1_q_2, register_1_q}), .clk(clk), .clr(reset));  // open: en
  Adder #(.width(30)) adder_1 (
    .a({register_1_q_3, register_1_q_2, register_1_q}), .b(30'h1), .out(adder_1_out));  // open: cin, cout
  ROM #(.addrWidth(5), .dataWidth(32)) rom_1 (.addr(register_1_q), .data(Instr));  // open: sel
  assign bit_extender_1_out = {{14{Instr[15]}}, Instr[15:0]};  // Bit_Extender bit_extender_1
  Adder #(.width(30)) adder_2 (.a(adder_1_out), .b(bit_extender_1_out), .out(adder_2_out));  // open: cin, cout
  Multiplexer #(.width(30)) multiplexer_1 (
    .in0(adder_1_out), .in1(adder_2_out), .out(multiplexer_1_out), .sel(or_1_out));  // open: en
  or or_1 (or_1_out, Ifbeq, zero);

  // Notes on the sheet:
  //   contents of rom_1 (hex, n*v repeats v):
  //   34080001 34090003 ac082000 8c0a2000 1485821 12a6023 3c0d0003 116c0002 1284023 34090005 34100006
  //   ac102020 8c112000 2099023 11300001 3c100003 14b9821 8c142020 34150006 274a821
endmodule

module Controller (
  input  [5:0] op,
  input  [5:0] func,
  output RegDst,
  output ALUSrc,
  output MemtoReg,
  output RegWrite,
  output [1:0] Extop,
  output MemWrite,
  output Branch,
  output [1:0] ALUop
);

  wire addu_out, beq_out, not_1_out, not_3_out, not_4_out, not_5_out, not_6_out, not_7_out, not_8_out,
       not_9_out, not_10_out, not_11_out, ori_out, subu_out;

  not not_1 (not_1_out, func[4]);
  // NOT_Gate not_2 has open pins: in=func[5], out=open
  not not_3 (not_3_out, func[3]);
  not not_4 (not_4_out, func[2]);
  not not_5 (not_5_out, func[1]);
  not not_6 (not_6_out, op[5]);
  not not_7 (not_7_out, op[4]);
  not not_8 (not_8_out, op[2]);
  not not_9 (not_9_out, op[3]);
  not not_10 (not_10_out, op[1]);
  not not_11 (not_11_out, op[0]);
  and addu (addu_out, func[5], not_1_out, not_6_out, not_7_out, not_9_out, not_3_out, not_10_out, not_11_out, not_8_out, not_4_out, not_5_out, func[0]);
  and subu (subu_out, func[5], not_1_out, not_3_out, not_6_out, not_7_out, not_9_out, not_8_out, not_10_out, not_11_out, not_4_out, func[1], func[0]);
  and ori (ori_out, not_6_out, not_7_out, op[3], op[2], not_10_out, op[0]);
  and lw (MemtoReg, op[5], not_7_out, not_9_out, not_8_out, op[1], op[0]);
  and sw (MemWrite, op[5], not_7_out, op[3], not_8_out, op[1], op[0]);
  and beq (beq_out, not_6_out, not_7_out, not_9_out, op[2], not_10_out, not_11_out);
  and lui (Extop[1], not_6_out, not_7_out, op[3], op[2], op[1], op[0]);
  or or_1 (RegDst, addu_out, subu_out);
  or or_2 (ALUSrc, ori_out, MemtoReg, MemWrite, Extop[1]);
  or or_3 (RegWrite, addu_out, subu_out, ori_out, MemtoReg, Extop[1]);
  or or_4 (Extop[0], MemWrite, MemtoReg);
  buf or_5 (Branch, beq_out);  // OR_Gate
  or or_6 (ALUop[1], ori_out, Extop[1]);
  or or_7 (ALUop[0], beq_out, subu_out);
endmodule

module GPR (
  input  [31:0] WD,
  input  [4:0] A1,
  input  [4:0] A2,
  input  WE,
  input  [4:0] A3,
  input  reset,
  output [31:0] RD1,
  output [31:0] RD2
);

  wire _01, _02, _03, _04, _05, _06, _07, _08, _09, _10, _11, _12, _13, _14, _15, _16, _17, _18, _19, _20,
       _21, _22, _23, _24, _25, _26, _27, _28, _29, _30, _31, _32, clock_1_out;
  wire [31:0] q01, q02, q03, q04, q05, q06, q07, q08, q09, q10, q11, q12, q13, q14, q15, q16, q17, q18, q19,
       q20, q21, q22, q23, q24, q25, q26, q27, q28, q29, q30, q31, q32;

  Clock clock_1 (.out(clock_1_out));
  Register #(.width(32)) register_1 (.D(WD), .en(_01), .Q(q01), .clk(clock_1_out), .clr(reset));
  Register #(.width(32)) register_2 (.D(WD), .en(_05), .Q(q05), .clk(clock_1_out), .clr(reset));
  Register #(.width(32)) register_3 (.D(WD), .en(_09), .Q(q09), .clk(clock_1_out), .clr(reset));
  Register #(.width(32)) register_4 (.D(WD), .en(_13), .Q(q13), .clk(clock_1_out), .clr(reset));
  Register #(.width(32)) register_5 (.D(WD), .en(_17), .Q(q17), .clk(clock_1_out), .clr(reset));
  Register #(.width(32)) register_6 (.D(WD), .en(_21), .Q(q21), .clk(clock_1_out), .clr(reset));
  Register #(.width(32)) register_7 (.D(WD), .en(_25), .Q(q25), .clk(clock_1_out), .clr(reset));
  Register #(.width(32)) register_8 (.D(WD), .en(_29), .Q(q29), .clk(clock_1_out), .clr(reset));
  Register #(.width(32)) register_9 (.D(WD), .en(_02), .Q(q02), .clk(clock_1_out), .clr(reset));
  Register #(.width(32)) register_10 (.D(WD), .en(_06), .Q(q06), .clk(clock_1_out), .clr(reset));
  Register #(.width(32)) register_11 (.D(WD), .en(_10), .Q(q10), .clk(clock_1_out), .clr(reset));
  Register #(.width(32)) register_12 (.D(WD), .en(_14), .Q(q14), .clk(clock_1_out), .clr(reset));
  Register #(.width(32)) register_13 (.D(WD), .en(_18), .Q(q18), .clk(clock_1_out), .clr(reset));
  Register #(.width(32)) register_14 (.D(WD), .en(_22), .Q(q22), .clk(clock_1_out), .clr(reset));
  Register #(.width(32)) register_15 (.D(WD), .en(_26), .Q(q26), .clk(clock_1_out), .clr(reset));
  Register #(.width(32)) register_16 (.D(WD), .en(_30), .Q(q30), .clk(clock_1_out), .clr(reset));
  Register #(.width(32)) register_17 (.D(WD), .en(_03), .Q(q03), .clk(clock_1_out), .clr(reset));
  Register #(.width(32)) register_18 (.D(WD), .en(_07), .Q(q07), .clk(clock_1_out), .clr(reset));
  Register #(.width(32)) register_19 (.D(WD), .en(_11), .Q(q11), .clk(clock_1_out), .clr(reset));
  Register #(.width(32)) register_20 (.D(WD), .en(_15), .Q(q15), .clk(clock_1_out), .clr(reset));
  Register #(.width(32)) register_21 (.D(WD), .en(_19), .Q(q19), .clk(clock_1_out), .clr(reset));
  Register #(.width(32)) register_22 (.D(WD), .en(_23), .Q(q23), .clk(clock_1_out), .clr(reset));
  Register #(.width(32)) register_23 (.D(WD), .en(_27), .Q(q27), .clk(clock_1_out), .clr(reset));
  Register #(.width(32)) register_24 (.D(WD), .en(_31), .Q(q31), .clk(clock_1_out), .clr(reset));
  Register #(.width(32)) register_25 (.D(WD), .en(_04), .Q(q04), .clk(clock_1_out), .clr(reset));
  Register #(.width(32)) register_26 (.D(WD), .en(_08), .Q(q08), .clk(clock_1_out), .clr(reset));
  Register #(.width(32)) register_27 (.D(WD), .en(_12), .Q(q12), .clk(clock_1_out), .clr(reset));
  Register #(.width(32)) register_28 (.D(WD), .en(_16), .Q(q16), .clk(clock_1_out), .clr(reset));
  Register #(.width(32)) register_29 (.D(WD), .en(_20), .Q(q20), .clk(clock_1_out), .clr(reset));
  Register #(.width(32)) register_30 (.D(WD), .en(_24), .Q(q24), .clk(clock_1_out), .clr(reset));
  Register #(.width(32)) register_31 (.D(WD), .en(_28), .Q(q28), .clk(clock_1_out), .clr(reset));
  Register #(.width(32)) register_32 (.D(WD), .en(_32), .Q(q32), .clk(clock_1_out), .clr(reset));
  Demultiplexer #(.select(5)) demultiplexer_1 (
    .out0(_01), .out1(_02), .out2(_03), .out3(_04), .out4(_05), .out5(_06), .out6(_07), .out7(_08),
    .out8(_09), .out9(_10), .out10(_11), .out11(_12), .out12(_13), .out13(_14), .out14(_15), .out15(_16),
    .out16(_17), .out17(_18), .out18(_19), .out19(_20), .out20(_21), .out21(_22), .out22(_23), .out23(_24),
    .out24(_25), .out25(_26), .out26(_27), .out27(_28), .out28(_29), .out29(_30), .out30(_31), .out31(_32),
    .in(WE), .sel(A3));  // open: en
  Multiplexer #(.select(5), .width(32)) multiplexer_1 (
    .in0(q01), .in1(q02), .in2(q03), .in3(q04), .in4(q05), .in5(q06), .in6(q07), .in7(q08), .in8(q09),
    .in9(q10), .in10(q11), .in11(q12), .in12(q13), .in13(q14), .in14(q15), .in15(q16), .in16(q17),
    .in17(q18), .in18(q19), .in19(q20), .in20(q21), .in21(q22), .in22(q23), .in23(q24), .in24(q25),
    .in25(q26), .in26(q27), .in27(q28), .in28(q29), .in29(q30), .in30(q31), .in31(q32), .out(RD1), .sel(A1));  // open: en
  Multiplexer #(.select(5), .width(32)) multiplexer_2 (
    .in0(q01), .in1(q02), .in2(q03), .in3(q04), .in4(q05), .in5(q06), .in6(q07), .in7(q08), .in8(q09),
    .in9(q10), .in10(q11), .in11(q12), .in12(q13), .in13(q14), .in14(q15), .in15(q16), .in16(q17),
    .in17(q18), .in18(q19), .in19(q20), .in20(q21), .in21(q22), .in22(q23), .in23(q24), .in24(q25),
    .in25(q26), .in26(q27), .in27(q28), .in28(q29), .in29(q30), .in30(q31), .in31(q32), .out(RD2), .sel(A2));  // open: en
endmodule

module ALU (
  input  [31:0] inputA,
  input  [31:0] inputB,
  input  [1:0] ALUOp,
  output [31:0] result,
  output zero
);

  wire [31:0] ADD_s, \n32bit减法器_用1bit减法器做_1_s , OR_c;

  \_32bit加法器  ADD (.S(ADD_s), .B(inputB), .A(inputA), .Cin(1'b0));  // open: Cout
  \_32bit减法器_用1bit减法器做  \u_32bit减法器_用1bit减法器做_1  (
    .S(\n32bit减法器_用1bit减法器做_1_s ), .A(inputA), .B(inputB), .Ci_1(1'b0));  // open: Ci
  \_32bit按位或  OR (.A(inputA), .B(inputB), .C(OR_c));
  Multiplexer #(.select(2), .width(32)) multiplexer_1 (
    .in0(ADD_s), .in1(\n32bit减法器_用1bit减法器做_1_s ), .in2(OR_c), .out(result), .sel(ALUOp));  // open: in3, en
  nor nor_1 (zero, result[0], result[1], result[2], result[3], result[4], result[5], result[6], result[7], result[8], result[9], result[10], result[11], result[12], result[13], result[14], result[16], result[17], result[18], result[19], result[20], result[21], result[22], result[23], result[24], result[25], result[26], result[27], result[28], result[29], result[30], result[31]);
endmodule

// EXT
module Extender (
  input  [15:0] input16,
  input  [1:0] Extop,
  output [31:0] output32
);

  wire [31:0] bit_extender_1_out, bit_extender_2_out;

  assign bit_extender_1_out = {{16{1'b0}}, input16};  // Bit_Extender bit_extender_1
  assign bit_extender_2_out = {{16{1'b0}}, input16};  // Bit_Extender bit_extender_2
  Multiplexer #(.select(2), .width(32)) multiplexer_1 (
    .in0(bit_extender_1_out), .in1(bit_extender_2_out), .in2({input16, {16{1'b0}}}), .out(output32),
    .sel(Extop));  // open: in3, en
endmodule
