// Logisim project MIPS-Lite2.circ as structural Verilog: 12 circuits, main circuit main
module main (
  input  in_1
);

  wire ALUSrc, bgez, clk, controller_1_memwrite, controller_1_regwrite, Mem2Reg, nPC_sel, RegDst;
  wire [1:0] controller_1_aluop_2_0, controller_1_extop_1_0;
  wire [4:0] multiplexer_1_out;
  wire [31:0] extender_1_ext32, ifu_1_instr, multiplexer_2_out, multiplexer_3_out, ram_1_data, regfile_1_rd1,
       regfile_1_rd2, zero;

  Clock clock_1 (.out(clk));
  // Probe on ifu_1_instr[31:26]
  // Probe on ifu_1_instr[5:0]
  IFU ifu_1 (.clk(clk), .reset(in_1), .Zero(zero), .Instr(ifu_1_instr), .nPC_sel(nPC_sel), .bgez(bgez));
  // Probe on ifu_1_instr
  Multiplexer #(.width(5)) multiplexer_1 (
    .in0(ifu_1_instr[20:16]), .in1(ifu_1_instr[15:11]), .out(multiplexer_1_out), .sel(RegDst));  // open: en
  Controller controller_1 (
    .OpCode(ifu_1_instr[31:26]), .Funct(ifu_1_instr[5:0]), .RegDst(RegDst), .ALUSrc(ALUSrc),
    .Mem2Reg(Mem2Reg), .RegWrite(controller_1_regwrite), .MemWrite(controller_1_memwrite), .nPC_Sel(nPC_sel),
    .Extop_1_0(controller_1_extop_1_0), .ALUOp_2_0(controller_1_aluop_2_0), .bgez_2(bgez),
    .bgez(ifu_1_instr[20:16]));
  Extender extender_1 (.Imm16(ifu_1_instr[15:0]), .Extop(controller_1_extop_1_0), .ext32(extender_1_ext32));
  RegFile regfile_1 (
    .A1(ifu_1_instr[25:21]), .A2(ifu_1_instr[20:16]), .A3(multiplexer_1_out), .WD(multiplexer_3_out),
    .RD2(regfile_1_rd2), .RD1(regfile_1_rd1), .clk(clk), .WE(controller_1_regwrite));
  Multiplexer #(.width(32)) multiplexer_2 (
    .in0(regfile_1_rd2), .in1(extender_1_ext32), .out(multiplexer_2_out), .sel(ALUSrc));  // open: en
  Multiplexer #(.width(32)) multiplexer_3 (
    .in0(zero), .in1(ram_1_data), .out(multiplexer_3_out), .sel(Mem2Reg));  // open: en
  ALU alu_1 (.A(regfile_1_rd1), .B(multiplexer_2_out), .in_4(controller_1_aluop_2_0), .C(zero), .bgez(bgez));
  RAM #(.addrWidth(5), .dataWidth(32), .bus("separate")) ram_1 (
    .addr(zero[6:2]), .din(regfile_1_rd2), .data(ram_1_data), .str(controller_1_memwrite), .clk(clk));  // open: sel, ld, clr

  // Other names for the same wires on the sheet: reset = in_1
endmodule

// GPR
module RegFile (
  input  clk,
  input  WE,
  input  [4:0] A1,
  input  [4:0] A2,
  input  [4:0] A3,
  input  [31:0] WD,
  output [31:0] RD2,
  output [31:0] RD1
);

  wire demultiplexer_1_out0, demultiplexer_1_out1, demultiplexer_1_out2, demultiplexer_1_out3,
       demultiplexer_1_out4, demultiplexer_1_out5, demultiplexer_1_out6, demultiplexer_1_out7,
       demultiplexer_1_out8, demultiplexer_1_out9, demultiplexer_1_out10, demultiplexer_1_out11,
       demultiplexer_1_out12, demultiplexer_1_out13, demultiplexer_1_out14, demultiplexer_1_out15,
       demultiplexer_1_out16, demultiplexer_1_out17, demultiplexer_1_out18, demultiplexer_1_out19,
       demultiplexer_1_out20, demultiplexer_1_out21, demultiplexer_1_out22, demultiplexer_1_out23,
       demultiplexer_1_out24, demultiplexer_1_out25, demultiplexer_1_out26, demultiplexer_1_out27,
       demultiplexer_1_out28, demultiplexer_1_out29, demultiplexer_1_out30, demultiplexer_1_out31;
  wire [31:0] _0, _1, _2, _3, _4, _5, _6, _7, _8, _9, _10, _11, _12, _13, _14, _15, _16, _17, _18, _19, _20,
       _21, _22, _23, _24, _25, _26, _27, _28, _29, _30, _31;

  Demultiplexer #(.select(5)) demultiplexer_1 (
    .out0(demultiplexer_1_out0), .out1(demultiplexer_1_out1), .out2(demultiplexer_1_out2),
    .out3(demultiplexer_1_out3), .out4(demultiplexer_1_out4), .out5(demultiplexer_1_out5),
    .out6(demultiplexer_1_out6), .out7(demultiplexer_1_out7), .out8(demultiplexer_1_out8),
    .out9(demultiplexer_1_out9), .out10(demultiplexer_1_out10), .out11(demultiplexer_1_out11),
    .out12(demultiplexer_1_out12), .out13(demultiplexer_1_out13), .out14(demultiplexer_1_out14),
    .out15(demultiplexer_1_out15), .out16(demultiplexer_1_out16), .out17(demultiplexer_1_out17),
    .out18(demultiplexer_1_out18), .out19(demultiplexer_1_out19), .out20(demultiplexer_1_out20),
    .out21(demultiplexer_1_out21), .out22(demultiplexer_1_out22), .out23(demultiplexer_1_out23),
    .out24(demultiplexer_1_out24), .out25(demultiplexer_1_out25), .out26(demultiplexer_1_out26),
    .out27(demultiplexer_1_out27), .out28(demultiplexer_1_out28), .out29(demultiplexer_1_out29),
    .out30(demultiplexer_1_out30), .out31(demultiplexer_1_out31), .in(WE), .sel(A3));  // open: en
  Register #(.width(32)) register_1 (.D(WD), .en(demultiplexer_1_out0), .Q(_0), .clk(clk));  // open: clr
  Register #(.width(32)) register_2 (.D(WD), .en(demultiplexer_1_out1), .Q(_1), .clk(clk));  // open: clr
  Register #(.width(32)) register_3 (.D(WD), .en(demultiplexer_1_out2), .Q(_2), .clk(clk));  // open: clr
  Register #(.width(32)) register_4 (.D(WD), .en(demultiplexer_1_out3), .Q(_3), .clk(clk));  // open: clr
  Register #(.width(32)) register_5 (.D(WD), .en(demultiplexer_1_out4), .Q(_4), .clk(clk));  // open: clr
  Register #(.width(32)) register_6 (.D(WD), .en(demultiplexer_1_out5), .Q(_5), .clk(clk));  // open: clr
  Register #(.width(32)) register_7 (.D(WD), .en(demultiplexer_1_out6), .Q(_6), .clk(clk));  // open: clr
  Register #(.width(32)) register_8 (.D(WD), .en(demultiplexer_1_out7), .Q(_7), .clk(clk));  // open: clr
  Register #(.width(32)) register_9 (.D(WD), .en(demultiplexer_1_out8), .Q(_8), .clk(clk));  // open: clr
  Register #(.width(32)) register_10 (.D(WD), .en(demultiplexer_1_out9), .Q(_9), .clk(clk));  // open: clr
  Register #(.width(32)) register_11 (.D(WD), .en(demultiplexer_1_out10), .Q(_10), .clk(clk));  // open: clr
  Register #(.width(32)) register_12 (.D(WD), .en(demultiplexer_1_out11), .Q(_11), .clk(clk));  // open: clr
  Register #(.width(32)) register_13 (.D(WD), .en(demultiplexer_1_out12), .Q(_12), .clk(clk));  // open: clr
  Register #(.width(32)) register_14 (.D(WD), .en(demultiplexer_1_out13), .Q(_13), .clk(clk));  // open: clr
  Register #(.width(32)) register_15 (.D(WD), .en(demultiplexer_1_out14), .Q(_14), .clk(clk));  // open: clr
  Register #(.width(32)) register_16 (.D(WD), .en(demultiplexer_1_out15), .Q(_15), .clk(clk));  // open: clr
  Register #(.width(32)) register_17 (.D(WD), .en(demultiplexer_1_out16), .Q(_16), .clk(clk));  // open: clr
  Register #(.width(32)) register_18 (.D(WD), .en(demultiplexer_1_out17), .Q(_17), .clk(clk));  // open: clr
  Register #(.width(32)) register_19 (.D(WD), .en(demultiplexer_1_out18), .Q(_18), .clk(clk));  // open: clr
  Register #(.width(32)) register_20 (.D(WD), .en(demultiplexer_1_out19), .Q(_19), .clk(clk));  // open: clr
  Register #(.width(32)) register_21 (.D(WD), .en(demultiplexer_1_out20), .Q(_20), .clk(clk));  // open: clr
  Register #(.width(32)) register_22 (.D(WD), .en(demultiplexer_1_out21), .Q(_21), .clk(clk));  // open: clr
  Register #(.width(32)) register_23 (.D(WD), .en(demultiplexer_1_out22), .Q(_22), .clk(clk));  // open: clr
  Register #(.width(32)) register_24 (.D(WD), .en(demultiplexer_1_out23), .Q(_23), .clk(clk));  // open: clr
  Register #(.width(32)) register_25 (.D(WD), .en(demultiplexer_1_out24), .Q(_24), .clk(clk));  // open: clr
  Register #(.width(32)) register_26 (.D(WD), .en(demultiplexer_1_out25), .Q(_25), .clk(clk));  // open: clr
  Register #(.width(32)) register_27 (.D(WD), .en(demultiplexer_1_out26), .Q(_26), .clk(clk));  // open: clr
  Register #(.width(32)) register_28 (.D(WD), .en(demultiplexer_1_out27), .Q(_27), .clk(clk));  // open: clr
  Register #(.width(32)) register_29 (.D(WD), .en(demultiplexer_1_out28), .Q(_28), .clk(clk));  // open: clr
  Register #(.width(32)) register_30 (.D(WD), .en(demultiplexer_1_out29), .Q(_29), .clk(clk));  // open: clr
  Register #(.width(32)) register_31 (.D(WD), .en(demultiplexer_1_out30), .Q(_30), .clk(clk));  // open: clr
  Register #(.width(32)) register_32 (.D(WD), .en(demultiplexer_1_out31), .Q(_31), .clk(clk));  // open: clr
  Multiplexer #(.select(5), .width(32)) multiplexer_1 (
    .in0(_0), .in1(_1), .in2(_2), .in3(_3), .in4(_4), .in5(_5), .in6(_6), .in7(_7), .in8(_8), .in9(_9),
    .in10(_10), .in11(_11), .in12(_12), .in13(_13), .in14(_14), .in15(_15), .in16(_16), .in17(_17),
    .in18(_18), .in19(_19), .in20(_20), .in21(_21), .in22(_22), .in23(_23), .in24(_24), .in25(_25),
    .in26(_26), .in27(_27), .in28(_28), .in29(_29), .in30(_30), .in31(_31), .out(RD2), .sel(A2));  // open: en
  Multiplexer #(.select(5), .width(32)) multiplexer_2 (
    .in0(_0), .in1(_1), .in2(_2), .in3(_3), .in4(_4), .in5(_5), .in6(_6), .in7(_7), .in8(_8), .in9(_9),
    .in10(_10), .in11(_11), .in12(_12), .in13(_13), .in14(_14), .in15(_15), .in16(_16), .in17(_17),
    .in18(_18), .in19(_19), .in20(_20), .in21(_21), .in22(_22), .in23(_23), .in24(_24), .in25(_25),
    .in26(_26), .in27(_27), .in28(_28), .in29(_29), .in30(_30), .in31(_31), .out(RD1), .sel(A1));  // open: en
endmodule

module ALU (
  input  [31:0] A,
  input  [31:0] B,
  input  bgez,
  input  [1:0] in_4,
  output [31:0] C
);

  wire [31:0] multiplexer_1_out, n32bit_adder_1_c, n32bit_ori_1_out_3, n32bit_subtract_1_out_3;

  Multiplexer #(.width(32)) multiplexer_1 (.in0(B), .in1({32{1'b0}}), .out(multiplexer_1_out), .sel(bgez));  // open: en
  _32bit_ADDer u_32bit_adder_1 (.C(n32bit_adder_1_c), .A(A), .B(B));
  _32bit_Subtract u_32bit_subtract_1 (.in_1(A), .in_2(multiplexer_1_out), .out_3(n32bit_subtract_1_out_3));
  _32bit_ori u_32bit_ori_1 (.in_1(A), .in_2(B), .out_3(n32bit_ori_1_out_3));
  Multiplexer #(.select(2), .width(32)) multiplexer_2 (
    .in0(n32bit_adder_1_c), .in1(n32bit_subtract_1_out_3), .in2(n32bit_ori_1_out_3), .out(C), .sel(in_4));  // open: in3, en
endmodule

module Controller (
  input  [4:0] bgez,
  input  [5:0] Funct,
  input  [5:0] OpCode,
  output bgez_2,
  output RegDst,
  output ALUSrc,
  output Mem2Reg,
  output RegWrite,
  output MemWrite,
  output nPC_Sel,
  output [1:0] Extop_1_0,
  output [1:0] ALUOp_2_0
);

  wire addu_out, beq_out, lw_out, not_1_out, not_2_out, not_3_out, not_4_out, not_5_out, not_6_out,
       not_7_out, not_8_out, not_9_out, not_10_out, not_11_out, not_12_out, not_13_out, not_14_out,
       not_15_out, not_16_out, not_17_out, ori_out, subu_out, sw_out;

  not not_1 (not_1_out, Funct[5]);
  not not_2 (not_2_out, Funct[4]);
  not not_3 (not_3_out, Funct[3]);
  not not_4 (not_4_out, Funct[2]);
  not not_5 (not_5_out, Funct[1]);
  not not_6 (not_6_out, Funct[0]);
  not not_7 (not_7_out, OpCode[5]);
  not not_8 (not_8_out, OpCode[4]);
  not not_9 (not_9_out, OpCode[3]);
  not not_10 (not_10_out, OpCode[2]);
  not not_11 (not_11_out, OpCode[1]);
  not not_12 (not_12_out, OpCode[0]);
  not not_13 (not_13_out, bgez[4]);
  not not_14 (not_14_out, bgez[3]);
  not not_15 (not_15_out, bgez[1]);
  not not_16 (not_16_out, bgez[2]);
  not not_17 (not_17_out, bgez[0]);
  and addu (addu_out, not_7_out, not_8_out, not_9_out, not_10_out, not_11_out, not_12_out, Funct[5], not_2_out, not_3_out, not_4_out, not_5_out, Funct[0]);
  and subu (subu_out, not_7_out, not_8_out, not_9_out, not_10_out, not_11_out, not_12_out, Funct[5], not_2_out, not_3_out, not_4_out, Funct[1], Funct[0]);
  and ori (ori_out, not_7_out, not_8_out, OpCode[3], OpCode[2], not_11_out, OpCode[0]);
  and lw (lw_out, OpCode[5], not_8_out, not_9_out, not_10_out, OpCode[1], OpCode[0]);
  and sw (sw_out, OpCode[5], not_8_out, OpCode[3], not_10_out, OpCode[1], OpCode[0]);
  and beq (beq_out, not_7_out, not_8_out, not_9_out, OpCode[2], not_11_out, not_12_out);
  and lui (Extop_1_0[1], not_7_out, not_8_out, OpCode[3], OpCode[2], OpCode[1], OpCode[0]);
  and u_bgez (bgez_2, not_7_out, not_8_out, not_9_out, not_10_out, not_11_out, OpCode[0], not_13_out, not_14_out, not_16_out, not_15_out, bgez[0]);
  or u_RegDst (RegDst, addu_out, subu_out);
  or u_ALUSrc (ALUSrc, ori_out, lw_out, sw_out, Extop_1_0[1]);
  buf u_Mem2Reg (Mem2Reg, lw_out);  // OR_Gate
  or u_RegWrite (RegWrite, addu_out, subu_out, ori_out, lw_out, Extop_1_0[1]);
  buf u_MemWrite (MemWrite, sw_out);  // OR_Gate
  buf u_nPC_Sel (nPC_Sel, beq_out);  // OR_Gate
  or Extop_0 (Extop_1_0[0], lw_out, sw_out);
  // OR_Gate add has open pins: in0=addu_out, in1=lw_out, in2=sw_out, out=open
  or sub (ALUOp_2_0[0], subu_out, beq_out, bgez_2);
  or \or  (ALUOp_2_0[1], ori_out, Extop_1_0[1]);
endmodule

module IFU (
  input  bgez,
  input  nPC_sel,
  input  clk,
  input  reset,
  input  [31:0] Zero,
  output [31:0] Instr
);

  wire _0, and_2_out, and_3_out, not_2_out, not_3_out, not_4_out, not_5_out, not_6_out, not_7_out, not_8_out,
       not_9_out, not_10_out, not_11_out, not_12_out, not_13_out, not_14_out, not_15_out, not_16_out,
       not_17_out, not_18_out, not_19_out, not_20_out, not_21_out, not_22_out, not_23_out, not_24_out,
       not_25_out, not_26_out, not_27_out, not_28_out, not_29_out, not_30_out, not_31_out, not_32_out,
       not_33_out, or_1_out, zero_t;
  wire [29:0] multiplexer_1_out, register_1_q;
  wire [31:0] bit_extender_1_out, n32bit_adder_2_c, PC_4_Offset;

  not not_1 (_0, Zero[31]);
  not not_2 (not_2_out, Zero[0]);
  not not_3 (not_3_out, Zero[1]);
  not not_4 (not_4_out, Zero[2]);
  not not_5 (not_5_out, Zero[3]);
  not not_6 (not_6_out, Zero[4]);
  not not_7 (not_7_out, Zero[5]);
  not not_8 (not_8_out, Zero[6]);
  not not_9 (not_9_out, Zero[7]);
  not not_10 (not_10_out, Zero[8]);
  not not_11 (not_11_out, Zero[9]);
  not not_12 (not_12_out, Zero[10]);
  not not_13 (not_13_out, Zero[11]);
  not not_14 (not_14_out, Zero[12]);
  not not_15 (not_15_out, Zero[13]);
  not not_16 (not_16_out, Zero[14]);
  not not_17 (not_17_out, Zero[15]);
  not not_18 (not_18_out, Zero[16]);
  not not_19 (not_19_out, Zero[17]);
  not not_20 (not_20_out, Zero[18]);
  not not_21 (not_21_out, Zero[19]);
  not not_22 (not_22_out, Zero[20]);
  not not_23 (not_23_out, Zero[21]);
  not not_24 (not_24_out, Zero[22]);
  not not_25 (not_25_out, Zero[23]);
  not not_26 (not_26_out, Zero[24]);
  not not_27 (not_27_out, Zero[25]);
  not not_28 (not_28_out, Zero[26]);
  not not_29 (not_29_out, Zero[27]);
  not not_30 (not_30_out, Zero[28]);
  not not_31 (not_31_out, Zero[29]);
  not not_32 (not_32_out, Zero[30]);
  not not_33 (not_33_out, Zero[31]);
  and and_1 (zero_t, not_2_out, not_3_out, not_4_out, not_5_out, not_6_out, not_7_out, not_8_out, not_9_out, not_10_out, not_11_out, not_12_out, not_13_out, not_14_out, not_15_out, not_16_out, not_17_out, not_19_out, not_20_out, not_21_out, not_22_out, not_23_out, not_24_out, not_25_out, not_26_out, not_27_out, not_28_out, not_29_out, not_30_out, not_31_out, not_32_out, not_33_out, not_18_out);
  and and_2 (and_2_out, bgez, _0);
  and and_3 (and_3_out, nPC_sel, zero_t);
  or or_1 (or_1_out, and_2_out, and_3_out);
  Multiplexer #(.width(30)) multiplexer_1 (
    .in0(n32bit_adder_2_c[29:0]), .in1(PC_4_Offset[29:0]), .out(multiplexer_1_out), .sel(or_1_out));  // open: en
  assign bit_extender_1_out = {{16{Instr[15]}}, Instr[15:0]};  // Bit_Extender bit_extender_1
  _32bit_ADDer u_32bit_adder_1 (.C(PC_4_Offset), .A(n32bit_adder_2_c), .B(bit_extender_1_out));
  Register #(.width(30)) register_1 (.D(multiplexer_1_out), .Q(register_1_q), .clk(clk), .clr(reset));  // open: en
  ROM #(.addrWidth(5), .dataWidth(32)) rom_1 (.addr(register_1_q[4:0]), .data(Instr));  // open: sel
  _32bit_ADDer u_32bit_adder_2 (.C(n32bit_adder_2_c), .A({2'b00, register_1_q}), .B(32'h1));

  // Other names for the same wires on the sheet: j_sel = nPC_sel; Offset[15:0] = Instr[15:0]

  // Notes on the sheet:
  //   contents of rom_1 (hex, n*v repeats v):
  //   34010001 34020008 34100000 34110008 3c12aabb 12200009 ae120000 8e130000 2619821 ae130004 2619821
  //   2609021 2028021 2218823 621fff6 21
endmodule

module Extender (
  input  [15:0] Imm16,
  input  [1:0] Extop,
  output [31:0] ext32
);

  wire [31:0] bit_extender_1_out, bit_extender_2_out;

  assign bit_extender_1_out = {{16{1'b0}}, Imm16};  // Bit_Extender bit_extender_1
  assign bit_extender_2_out = {{16{Imm16[15]}}, Imm16};  // Bit_Extender bit_extender_2
  Multiplexer #(.select(2), .width(32)) multiplexer_1 (
    .in0(bit_extender_1_out), .in1(bit_extender_2_out), .in2({Imm16, {16{1'b0}}}), .out(ext32), .sel(Extop));  // open: in3, en
endmodule

// ADDer
module _32bit_ADDer (
  input  [31:0] A,
  input  [31:0] B,
  output [31:0] C
);

  wire com_1_bit_adder_2_c_i_1, com_1_bit_adder_3_c_i_1, com_1_bit_adder_4_c_i_1, com_1_bit_adder_5_c_i_1,
       com_1_bit_adder_6_c_i_1, com_1_bit_adder_7_c_i_1, com_1_bit_adder_8_c_i_1, com_1_bit_adder_9_c_i_1,
       com_1_bit_adder_10_c_i_1, com_1_bit_adder_11_c_i_1, com_1_bit_adder_12_c_i_1,
       com_1_bit_adder_13_c_i_1, com_1_bit_adder_14_c_i_1, com_1_bit_adder_15_c_i_1,
       com_1_bit_adder_16_c_i_1, com_1_bit_adder_17_c_i_1, com_1_bit_adder_18_c_i_1,
       com_1_bit_adder_19_c_i_1, com_1_bit_adder_20_c_i_1, com_1_bit_adder_21_c_i_1,
       com_1_bit_adder_22_c_i_1, com_1_bit_adder_23_c_i_1, com_1_bit_adder_24_c_i_1,
       com_1_bit_adder_25_c_i_1, com_1_bit_adder_26_c_i_1, com_1_bit_adder_27_c_i_1,
       com_1_bit_adder_28_c_i_1, com_1_bit_adder_29_c_i_1, com_1_bit_adder_30_c_i_1,
       com_1_bit_adder_31_c_i_1, n1_bit_adder_1_c;

  com_1_bit_ADDer com_1_bit_adder_1 (
    .a_i(A[31]), .b_i(B[31]), .c_i(com_1_bit_adder_2_c_i_1), .s_i(C[31]));  // open: c_i_1
  com_1_bit_ADDer com_1_bit_adder_2 (
    .a_i(A[30]), .b_i(B[30]), .c_i(com_1_bit_adder_3_c_i_1), .s_i(C[30]), .c_i_1(com_1_bit_adder_2_c_i_1));
  com_1_bit_ADDer com_1_bit_adder_3 (
    .a_i(A[29]), .b_i(B[29]), .c_i(com_1_bit_adder_4_c_i_1), .s_i(C[29]), .c_i_1(com_1_bit_adder_3_c_i_1));
  com_1_bit_ADDer com_1_bit_adder_4 (
    .a_i(A[28]), .b_i(B[28]), .c_i(com_1_bit_adder_5_c_i_1), .s_i(C[28]), .c_i_1(com_1_bit_adder_4_c_i_1));
  com_1_bit_ADDer com_1_bit_adder_5 (
    .a_i(A[27]), .b_i(B[27]), .c_i(com_1_bit_adder_6_c_i_1), .s_i(C[27]), .c_i_1(com_1_bit_adder_5_c_i_1));
  com_1_bit_ADDer com_1_bit_adder_6 (
    .a_i(A[26]), .b_i(B[26]), .c_i(com_1_bit_adder_7_c_i_1), .s_i(C[26]), .c_i_1(com_1_bit_adder_6_c_i_1));
  com_1_bit_ADDer com_1_bit_adder_7 (
    .a_i(A[25]), .b_i(B[25]), .c_i(com_1_bit_adder_8_c_i_1), .s_i(C[25]), .c_i_1(com_1_bit_adder_7_c_i_1));
  com_1_bit_ADDer com_1_bit_adder_8 (
    .a_i(A[24]), .b_i(B[24]), .c_i(com_1_bit_adder_9_c_i_1), .s_i(C[24]), .c_i_1(com_1_bit_adder_8_c_i_1));
  com_1_bit_ADDer com_1_bit_adder_9 (
    .a_i(A[23]), .b_i(B[23]), .c_i(com_1_bit_adder_10_c_i_1), .s_i(C[23]), .c_i_1(com_1_bit_adder_9_c_i_1));
  com_1_bit_ADDer com_1_bit_adder_10 (
    .a_i(A[22]), .b_i(B[22]), .c_i(com_1_bit_adder_11_c_i_1), .s_i(C[22]), .c_i_1(com_1_bit_adder_10_c_i_1));
  com_1_bit_ADDer com_1_bit_adder_11 (
    .a_i(A[21]), .b_i(B[21]), .c_i(com_1_bit_adder_12_c_i_1), .s_i(C[21]), .c_i_1(com_1_bit_adder_11_c_i_1));
  com_1_bit_ADDer com_1_bit_adder_12 (
    .a_i(A[20]), .b_i(B[20]), .c_i(com_1_bit_adder_13_c_i_1), .s_i(C[20]), .c_i_1(com_1_bit_adder_12_c_i_1));
  com_1_bit_ADDer com_1_bit_adder_13 (
    .a_i(A[19]), .b_i(B[19]), .c_i(com_1_bit_adder_14_c_i_1), .s_i(C[19]), .c_i_1(com_1_bit_adder_13_c_i_1));
  com_1_bit_ADDer com_1_bit_adder_14 (
    .a_i(A[18]), .b_i(B[18]), .c_i(com_1_bit_adder_15_c_i_1), .s_i(C[18]), .c_i_1(com_1_bit_adder_14_c_i_1));
  com_1_bit_ADDer com_1_bit_adder_15 (
    .a_i(A[17]), .b_i(B[17]), .c_i(com_1_bit_adder_16_c_i_1), .s_i(C[17]), .c_i_1(com_1_bit_adder_15_c_i_1));
  com_1_bit_ADDer com_1_bit_adder_16 (
    .a_i(A[16]), .b_i(B[16]), .c_i(com_1_bit_adder_17_c_i_1), .s_i(C[16]), .c_i_1(com_1_bit_adder_16_c_i_1));
  com_1_bit_ADDer com_1_bit_adder_17 (
    .a_i(A[15]), .b_i(B[15]), .c_i(com_1_bit_adder_18_c_i_1), .s_i(C[15]), .c_i_1(com_1_bit_adder_17_c_i_1));
  com_1_bit_ADDer com_1_bit_adder_18 (
    .a_i(A[14]), .b_i(B[14]), .c_i(com_1_bit_adder_19_c_i_1), .s_i(C[14]), .c_i_1(com_1_bit_adder_18_c_i_1));
  com_1_bit_ADDer com_1_bit_adder_19 (
    .a_i(A[13]), .b_i(B[13]), .c_i(com_1_bit_adder_20_c_i_1), .s_i(C[13]), .c_i_1(com_1_bit_adder_19_c_i_1));
  com_1_bit_ADDer com_1_bit_adder_20 (
    .a_i(A[12]), .b_i(B[12]), .c_i(com_1_bit_adder_21_c_i_1), .s_i(C[12]), .c_i_1(com_1_bit_adder_20_c_i_1));
  com_1_bit_ADDer com_1_bit_adder_21 (
    .a_i(A[11]), .b_i(B[11]), .c_i(com_1_bit_adder_22_c_i_1), .s_i(C[11]), .c_i_1(com_1_bit_adder_21_c_i_1));
  com_1_bit_ADDer com_1_bit_adder_22 (
    .a_i(A[10]), .b_i(B[10]), .c_i(com_1_bit_adder_23_c_i_1), .s_i(C[10]), .c_i_1(com_1_bit_adder_22_c_i_1));
  com_1_bit_ADDer com_1_bit_adder_23 (
    .a_i(A[9]), .b_i(B[9]), .c_i(com_1_bit_adder_24_c_i_1), .s_i(C[9]), .c_i_1(com_1_bit_adder_23_c_i_1));
  com_1_bit_ADDer com_1_bit_adder_24 (
    .a_i(A[8]), .b_i(B[8]), .c_i(com_1_bit_adder_25_c_i_1), .s_i(C[8]), .c_i_1(com_1_bit_adder_24_c_i_1));
  com_1_bit_ADDer com_1_bit_adder_25 (
    .a_i(A[7]), .b_i(B[7]), .c_i(com_1_bit_adder_26_c_i_1), .s_i(C[7]), .c_i_1(com_1_bit_adder_25_c_i_1));
  com_1_bit_ADDer com_1_bit_adder_26 (
    .a_i(A[6]), .b_i(B[6]), .c_i(com_1_bit_adder_27_c_i_1), .s_i(C[6]), .c_i_1(com_1_bit_adder_26_c_i_1));
  com_1_bit_ADDer com_1_bit_adder_27 (
    .a_i(A[5]), .b_i(B[5]), .c_i(com_1_bit_adder_28_c_i_1), .s_i(C[5]), .c_i_1(com_1_bit_adder_27_c_i_1));
  com_1_bit_ADDer com_1_bit_adder_28 (
    .a_i(A[4]), .b_i(B[4]), .c_i(com_1_bit_adder_29_c_i_1), .s_i(C[4]), .c_i_1(com_1_bit_adder_28_c_i_1));
  com_1_bit_ADDer com_1_bit_adder_29 (
    .a_i(A[3]), .b_i(B[3]), .c_i(com_1_bit_adder_30_c_i_1), .s_i(C[3]), .c_i_1(com_1_bit_adder_29_c_i_1));
  com_1_bit_ADDer com_1_bit_adder_30 (
    .a_i(A[2]), .b_i(B[2]), .c_i(com_1_bit_adder_31_c_i_1), .s_i(C[2]), .c_i_1(com_1_bit_adder_30_c_i_1));
  com_1_bit_ADDer com_1_bit_adder_31 (
    .a_i(A[1]), .b_i(B[1]), .c_i(n1_bit_adder_1_c), .s_i(C[1]), .c_i_1(com_1_bit_adder_31_c_i_1));
  _1_bit_ADDer u_1_bit_adder_1 (.s(C[0]), .c(n1_bit_adder_1_c), .a(A[0]), .b(B[0]));

  // Other names for the same wires on the sheet: s0 = C[0]; s1 = C[1]; s2 = C[2]; s3 = C[3]; s4 = C[4]; s5 = C[5];
  //   s6 = C[6]; s7 = C[7]; s8 = C[8]; s9 = C[9]; s10 = C[10]; s11 = C[11]; s12 = C[12]; s13 = C[13]; s14 = C[14];
  //   s15 = C[15]; s16 = C[16]; s17 = C[17]; s18 = C[18]; s19 = C[19]; s20 = C[20]; s21 = C[21]; s22 = C[22];
  //   s23 = C[23]; s24 = C[24]; s25 = C[25]; s26 = C[26]; s27 = C[27]; s28 = C[28]; s29 = C[29]; s30 = C[30];
  //   s31 = C[31]
endmodule

module ADDer_util (
  input  in_1,
  input  in_2,
  input  in_3,
  output out_4
);

  wire and_1_out, and_2_out, and_3_out;

  and and_1 (and_1_out, in_1, in_3);
  and and_2 (and_2_out, in_1, in_2);
  and and_3 (and_3_out, in_2, in_3);
  or or_1 (out_4, and_1_out, and_2_out, and_3_out);
endmodule

module _1_bit_ADDer (
  input  a,
  input  b,
  output s,
  output c
);

  xor xor_1 (s, a, b);
  and and_1 (c, a, b);
endmodule

module com_1_bit_ADDer (
  input  a_i,
  input  b_i,
  input  c_i,
  output s_i,
  output c_i_1
);

  xor xor_1 (s_i, a_i, b_i, c_i);
  ADDer_util adder_util_1 (.in_1(a_i), .in_2(b_i), .in_3(c_i), .out_4(c_i_1));
endmodule

// Sub
module _32bit_Subtract (
  input  [31:0] in_1,
  input  [31:0] in_2,
  output [31:0] out_3
);

  wire [31:0] n32bit_adder_1_c, not_1_out;

  assign not_1_out = ~in_2;  // NOT_Gate not_1, 32 bits wide
  _32bit_ADDer u_32bit_adder_1 (.C(n32bit_adder_1_c), .A(not_1_out), .B(32'h1));
  _32bit_ADDer u_32bit_adder_2 (.C(out_3), .A(in_1), .B(n32bit_adder_1_c));
endmodule

// Or
module _32bit_ori (
  input  [31:0] in_1,
  input  [31:0] in_2,
  output [31:0] out_3
);

  assign out_3 = in_1 | in_2;  // OR_Gate or_1, 32 bits wide
endmodule
